// Digital circuit aritimetica.dig as structural Verilog
module aritimetica (
  input  Cin,
  input  S0,
  input  S1,
  input  [15:0] Ai,
  input  [15:0] Bi,
  output [15:0] Gi,
  output Cot,
  output Ovf,
  output Neg
);

  wire add_1_c_o;
  wire [15:0] and_1_out, and_2_out, not_1_out, or_1_out;

  assign not_1_out = ~Bi;  // Not not_1, 16 bits wide
  assign and_1_out = {16{S0}} & Bi;  // And and_1, 16 bits wide
  assign and_2_out = {16{S1}} & not_1_out;  // And and_2, 16 bits wide
  assign or_1_out = and_1_out | and_2_out;  // Or or_1, 16 bits wide
  Add #(.Bits(15)) add_1 (.a(Ai[14:0]), .b(or_1_out[14:0]), .c_i(Cin), .s(Gi[14:0]), .c_o(add_1_c_o));
  Add add_2 (.a(Ai[15]), .b(or_1_out[15]), .c_i(add_1_c_o), .s(Gi[15]), .c_o(Cot));
  xor xor_1 (Ovf, add_1_c_o, Cot);

  assign Neg = Gi[15];

  // Notes on the sheet:
  //   Lucas Martins Soares
endmodule
