// Digital circuit data_path.dig as structural Verilog
module data_path (
  input  Clk,
  input  RW,
  input  [2:0] DA,
  input  [2:0] AA,
  input  [2:0] BA,
  input  MB,
  input  [3:0] Fs,
  input  MD,
  input  [15:0] Cst,
  input  [15:0] Data_in,
  output [15:0] Bus_A,
  output [15:0] Bus_B,
  output C,
  output V,
  output N,
  output Z,
  output [15:0] Out
);

  wire [15:0] function_unit_1_out, register_file_1_ulb;

  register_file register_file_1 (
    .LE(RW), .DS(DA), .Clk(Clk), .D(Out), .As(AA), .Bs(BA), .ULa(Bus_A), .ULb(register_file_1_ulb));
  Multiplexer #(.Bits(16)) multiplexer_1 (.sel(MB), .in_0(register_file_1_ulb), .in_1(Cst), .out(Bus_B));
  function_unit function_unit_1 (
    .Fs(Fs), .A(Bus_A), .B(Bus_B), .Cot(C), .Ovf(V), .Neg(N), .Z(Z), .Out(function_unit_1_out));
  Multiplexer #(.Bits(16)) multiplexer_2 (.sel(MD), .in_0(function_unit_1_out), .in_1(Data_in), .out(Out));

  // Notes on the sheet:
  //   Clk: Hz: 2
  //   Lucas Martins Soares
endmodule
