// Digital circuit extended.dig as structural Verilog
module extended (
  input  [2:0] _2a0,
  input  [2:0] _8a6,
  output [15:0] S
);

  BitExtender #(.inputBits(6)) bitextender_1 (.in({_8a6, _2a0}), .out(S));

  // Notes on the sheet:
  //   Lucas Martins Soares
endmodule
