// Digital circuit function_unit.dig as structural Verilog
module function_unit (
  input  [3:0] Fs,
  input  [15:0] A,
  input  [15:0] B,
  output Cot,
  output Ovf,
  output Neg,
  output Z,
  output [15:0] Out
);

  wire and_1_out;
  wire [15:0] shifter_1_h, ula_1_gi;

  ula ula_1 (.G_select(Fs), .Ai(A), .Bi(B), .Gi(ula_1_gi), .Cot(Cot), .Ovf(Ovf), .Neg(Neg));
  shifter shifter_1 (.S(Fs[1:0]), .B(B), .H(shifter_1_h));
  and and_1 (and_1_out, Fs[2], Fs[3]);
  zero zero_1 (.in(ula_1_gi), .out(Z));
  Multiplexer #(.Bits(16)) multiplexer_1 (.sel(and_1_out), .in_0(ula_1_gi), .in_1(shifter_1_h), .out(Out));

  // Notes on the sheet:
  //   Lucas Martins Soares
endmodule
