// Digital circuit instruction_decoder.dig as structural Verilog
module instruction_decoder (
  input  [15:0] Ist,
  output BC,
  output JB,
  output PL,
  output MW,
  output RW,
  output MD,
  output [3:0] FS,
  output MB,
  output [2:0] BA,
  output [2:0] AA,
  output [2:0] DA
);

  wire not_1_out, not_2_out;

  not not_1 (not_1_out, Ist[15]);
  and and_1 (PL, Ist[15], Ist[14]);
  and and_2 (MW, not_1_out, Ist[14]);
  not not_2 (not_2_out, PL);
  and and_3 (FS[0], not_2_out, Ist[9]);
  not not_3 (RW, Ist[14]);
  // Pins of 1 and 4 bits meet at {Ist[12:10], FS[0]}

  assign AA = Ist[5:3];
  assign BA = Ist[2:0];
  assign BC = Ist[9];
  assign DA = Ist[8:6];
  assign FS[3:1] = Ist[12:10];
  assign JB = Ist[13];
  assign MB = Ist[15];
  assign MD = Ist[13];

  // Notes on the sheet:
  //   Lucas Martins Soares
endmodule
