// Digital circuit logica.dig as structural Verilog
module logica (
  input  [15:0] Ai,
  input  [15:0] Bi,
  input  S0,
  input  S1,
  output [15:0] Gi
);

  wire [15:0] and_1_out, not_1_out, or_1_out, xor_1_out;

  assign and_1_out = Ai & Bi;  // And and_1, 16 bits wide
  assign or_1_out = Ai | Bi;  // Or or_1, 16 bits wide
  assign xor_1_out = Ai ^ Bi;  // XOr xor_1, 16 bits wide
  assign not_1_out = ~Ai;  // Not not_1, 16 bits wide
  Multiplexer #(.Selector_Bits(2), .Bits(16)) multiplexer_1 (
    .sel({S1, S0}), .in_0(and_1_out), .in_1(or_1_out), .in_2(xor_1_out), .in_3(not_1_out), .out(Gi));

  // Notes on the sheet:
  //   Lucas Martins Soares
endmodule
