// Digital circuit main.dig as structural Verilog
module main (
  input  clk,
  output [15:0] Bus_A,
  output [15:0] out_3,
  output [15:0] Bus_B,
  output [15:0] out_5,
  output [15:0] Out,
  output [2:0] out_7,
  output [2:0] out_8,
  output [15:0] out_9
);

  wire AA, BA, BC, branch_control_1_out, branch_control_1_ps, C, DA, FS, JB, MB, MD, MW, N, PL, RW, V, Z;
  wire [15:0] data_path_1_p1, multiplexer_1_out;

  branch_control branch_control_1 (
    .PL(PL), .JB(JB), .BC(BC), .Z(Z), .N(N), .PS(branch_control_1_ps), .Out(branch_control_1_out));
  // instruction_decoder instruction_decoder_1: pin names not known; wires that end beside it: DA, AA, BA, MB, FS, MD, RW, MW, PL, JB, out_3, BC
  pc pc_1 (.in(multiplexer_1_out), .ld(branch_control_1_out), .InS(branch_control_1_ps), .clk(clk), .out(out_5));
  ROM #(.AddrBits(16), .Bits(16)) rom_1 (.A(out_5), .sel(1'b1), .D(out_3));
  Multiplexer #(.Bits(16)) multiplexer_1 (
    .sel(branch_control_1_ps), .in_0(out_9), .in_1(Bus_A), .out(multiplexer_1_out));
  extended extended_1 (._2a0(out_3[2:0]), ._8a6(out_3[8:6]), .S(out_9));
  // data_path data_path_1: pin names not known; wires that end beside it: data_path_1_p1, {{13{1'b0}}, out_3[2:0]}, MD, FS, Out, MB, Z, BA, N, AA, V, DA, C, RW, Bus_B, clk, Bus_A
  RAMDualPort #(.AddrBits(16), .Bits(16)) ramdualport_1 (
    .A(Bus_A), .Din(Bus_B), .str(MW), .C(clk), .ld(1'b1), .D(data_path_1_p1));

  assign out_7 = out_3[2:0];
  assign out_8 = out_3[8:6];

  // Notes on the sheet:
  //   clk: Hz: 10
  //   Lucas Martins Soares
  //   contents of rom_1 (hex, n*v repeats v):
  //   9805,80,180,9843,9941,98c1,4b2,2d8,b18,c3e5,190,368,b29,c3e0,403a
endmodule
