// Digital circuit pc.dig as structural Verilog
module pc (
  input  [15:0] in,
  input  ld,
  input  InS,
  input  clk,
  output [15:0] out
);

  wire not_1_out;
  wire [15:0] add_1_s, multiplexer_1_out;

  Add #(.Bits(16)) add_1 (.a(out), .b(in), .c_i(1'b0), .s(add_1_s));  // open: c_o
  Multiplexer #(.Bits(16)) multiplexer_1 (.sel(InS), .in_0(add_1_s), .in_1(in), .out(multiplexer_1_out));
  not not_1 (not_1_out, ld);
  CounterPreset #(.Bits(16)) counterpreset_1 (
    .en(not_1_out), .C(clk), .dir(1'b0), .in(multiplexer_1_out), .ld(ld), .clr(1'b0), .out(out));  // open: ovf

  // Notes on the sheet:
  //   Lucas Martins Soares
endmodule
