// Digital circuit register_file.dig as structural Verilog
module register_file (
  input  LE,
  input  [2:0] DS,
  input  Clk,
  input  [15:0] D,
  input  [2:0] As,
  input  [2:0] Bs,
  output [15:0] ULa,
  output [15:0] ULb
);

  wire and_1_out, and_2_out, and_3_out, and_4_out, and_5_out, and_6_out, and_7_out, and_8_out,
       decoder_1_out_0, decoder_1_out_1, decoder_1_out_2, decoder_1_out_3, decoder_1_out_4, decoder_1_out_5,
       decoder_1_out_6, decoder_1_out_7;
  wire [15:0] register_1_q, register_2_q, register_3_q, register_4_q, register_5_q, register_6_q,
       register_7_q, register_8_q;

  Decoder #(.Selector_Bits(3)) decoder_1 (
    .sel(DS), .out_0(decoder_1_out_0), .out_1(decoder_1_out_1), .out_2(decoder_1_out_2),
    .out_3(decoder_1_out_3), .out_4(decoder_1_out_4), .out_5(decoder_1_out_5), .out_6(decoder_1_out_6),
    .out_7(decoder_1_out_7));
  and and_1 (and_1_out, decoder_1_out_0, LE);
  and and_2 (and_2_out, decoder_1_out_1, LE);
  and and_3 (and_3_out, decoder_1_out_2, LE);
  and and_4 (and_4_out, decoder_1_out_3, LE);
  and and_5 (and_5_out, decoder_1_out_4, LE);
  and and_6 (and_6_out, decoder_1_out_5, LE);
  and and_7 (and_7_out, decoder_1_out_6, LE);
  and and_8 (and_8_out, decoder_1_out_7, LE);
  Register #(.Bits(16)) register_1 (.D(D), .C(Clk), .en(and_1_out), .Q(register_1_q));
  Register #(.Bits(16)) register_2 (.D(D), .C(Clk), .en(and_2_out), .Q(register_2_q));
  Register #(.Bits(16)) register_3 (.D(D), .C(Clk), .en(and_3_out), .Q(register_3_q));
  Register #(.Bits(16)) register_4 (.D(D), .C(Clk), .en(and_4_out), .Q(register_4_q));
  Register #(.Bits(16)) register_5 (.D(D), .C(Clk), .en(and_5_out), .Q(register_5_q));
  Register #(.Bits(16)) register_6 (.D(D), .C(Clk), .en(and_6_out), .Q(register_6_q));
  Register #(.Bits(16)) register_7 (.D(D), .C(Clk), .en(and_7_out), .Q(register_7_q));
  Register #(.Bits(16)) register_8 (.D(D), .C(Clk), .en(and_8_out), .Q(register_8_q));
  Multiplexer #(.Selector_Bits(3), .Bits(16)) multiplexer_1 (
    .sel(As), .in_0(register_1_q), .in_1(register_2_q), .in_2(register_3_q), .in_3(register_4_q),
    .in_4(register_5_q), .in_5(register_6_q), .in_6(register_7_q), .in_7(register_8_q), .out(ULa));
  Multiplexer #(.Selector_Bits(3), .Bits(16)) multiplexer_2 (
    .sel(Bs), .in_0(register_1_q), .in_1(register_2_q), .in_2(register_3_q), .in_3(register_4_q),
    .in_4(register_5_q), .in_5(register_6_q), .in_6(register_7_q), .in_7(register_8_q), .out(ULb));

  // Notes on the sheet:
  //   Clk: Hz: 2
  //   Lucas Martins Soares
endmodule
