// Digital circuit shifter.dig as structural Verilog
module shifter (
  input  [1:0] S,
  input  [15:0] B,
  output [15:0] H
);

  Multiplexer #(.Selector_Bits(2)) multiplexer_1 (
    .sel(S), .in_0(B[0]), .in_1(B[1]), .in_2(B[15]), .in_3(1'b0), .out(H[0]));
  Multiplexer #(.Selector_Bits(2)) multiplexer_2 (
    .sel(S), .in_0(B[1]), .in_1(B[2]), .in_2(B[0]), .in_3(1'b0), .out(H[1]));
  Multiplexer #(.Selector_Bits(2)) multiplexer_3 (
    .sel(S), .in_0(B[2]), .in_1(B[3]), .in_2(B[1]), .in_3(1'b0), .out(H[2]));
  Multiplexer #(.Selector_Bits(2)) multiplexer_4 (
    .sel(S), .in_0(B[3]), .in_1(B[4]), .in_2(B[2]), .in_3(1'b0), .out(H[3]));
  Multiplexer #(.Selector_Bits(2)) multiplexer_5 (
    .sel(S), .in_0(B[4]), .in_1(B[5]), .in_2(B[3]), .in_3(1'b0), .out(H[4]));
  Multiplexer #(.Selector_Bits(2)) multiplexer_6 (
    .sel(S), .in_0(B[5]), .in_1(B[6]), .in_2(B[4]), .in_3(1'b0), .out(H[5]));
  Multiplexer #(.Selector_Bits(2)) multiplexer_7 (
    .sel(S), .in_0(B[6]), .in_1(B[7]), .in_2(B[5]), .in_3(1'b0), .out(H[6]));
  Multiplexer #(.Selector_Bits(2)) multiplexer_8 (
    .sel(S), .in_0(B[7]), .in_1(B[8]), .in_2(B[6]), .in_3(1'b0), .out(H[7]));
  Multiplexer #(.Selector_Bits(2)) multiplexer_9 (
    .sel(S), .in_0(B[8]), .in_1(B[9]), .in_2(B[7]), .in_3(1'b0), .out(H[8]));
  Multiplexer #(.Selector_Bits(2)) multiplexer_10 (
    .sel(S), .in_0(B[9]), .in_1(B[10]), .in_2(B[8]), .in_3(1'b0), .out(H[9]));
  Multiplexer #(.Selector_Bits(2)) multiplexer_11 (
    .sel(S), .in_0(B[10]), .in_1(B[9]), .in_2(B[11]), .in_3(1'b0), .out(H[10]));
  Multiplexer #(.Selector_Bits(2)) multiplexer_12 (
    .sel(S), .in_0(B[11]), .in_1(B[12]), .in_2(B[10]), .in_3(1'b0), .out(H[11]));
  Multiplexer #(.Selector_Bits(2)) multiplexer_13 (
    .sel(S), .in_0(B[12]), .in_1(B[13]), .in_2(B[11]), .in_3(1'b0), .out(H[12]));
  Multiplexer #(.Selector_Bits(2)) multiplexer_14 (
    .sel(S), .in_0(B[13]), .in_1(B[14]), .in_2(B[12]), .in_3(1'b0), .out(H[13]));
  Multiplexer #(.Selector_Bits(2)) multiplexer_15 (
    .sel(S), .in_0(B[14]), .in_1(B[15]), .in_2(B[13]), .in_3(1'b0), .out(H[14]));
  Multiplexer #(.Selector_Bits(2)) multiplexer_16 (
    .sel(S), .in_0(B[15]), .in_1(B[0]), .in_2(B[14]), .in_3(1'b0), .out(H[15]));

  // Notes on the sheet:
  //   Lucas Martins Soares
endmodule
