// Digital circuit ula.dig as structural Verilog
module ula (
  input  [3:0] G_select,
  input  [15:0] Ai,
  input  [15:0] Bi,
  output [15:0] Gi,
  output Cot,
  output Ovf,
  output Neg
);

  wire [15:0] aritimetica_1_gi, logica_1_gi;

  aritimetica aritimetica_1 (
    .Cin(G_select[0]), .S0(G_select[1]), .S1(G_select[2]), .Ai(Ai), .Bi(Bi), .Gi(aritimetica_1_gi),
    .Cot(Cot), .Ovf(Ovf), .Neg(Neg));
  logica logica_1 (.Ai(Ai), .Bi(Bi), .S0(G_select[0]), .S1(G_select[1]), .Gi(logica_1_gi));
  Multiplexer #(.Bits(16)) multiplexer_1 (.sel(G_select[3]), .in_0(aritimetica_1_gi), .in_1(logica_1_gi), .out(Gi));

  // Notes on the sheet:
  //   Lucas Martins Soares
endmodule
