// Digital circuit zero.dig as structural Verilog
module zero (
  input  [15:0] in,
  output out
);

  nor nor_1 (out, in[0], in[1], in[2], in[3], in[4], in[5], in[6], in[7], in[8], in[9], in[10], in[11], in[12], in[13], in[14], in[15]);

  // Notes on the sheet:
  //   Lucas Martins Soares
endmodule
